// Logisim project buildMux.circ as structural Verilog
module _2_1_MUX (
  input  in_0,
  input  in_1,
  input  select,
  output out
);

  wire and_1_out, and_2_out, not_1_out;

  not not_1 (not_1_out, select);
  and and_1 (and_1_out, in_0, not_1_out);
  or or_1 (out, and_1_out, and_2_out);
  and and_2 (and_2_out, in_1, select);
endmodule

module _4_1_MUX (
  input  in_00,
  input  in_01,
  input  in_10,
  input  in_11,
  input  sel_0,
  input  sel_1,
  output out
);

  wire n2_1_mux_1_out, n2_1_mux_2_out;

  _2_1_MUX u_2_1_mux_1 (.in_0(in_00), .in_1(in_01), .select(sel_1), .out(n2_1_mux_1_out));
  _2_1_MUX u_2_1_mux_2 (.in_0(in_10), .in_1(in_11), .select(sel_1), .out(n2_1_mux_2_out));
  _2_1_MUX u_2_1_mux_3 (.in_0(n2_1_mux_1_out), .in_1(n2_1_mux_2_out), .select(sel_0), .out(out));
endmodule
